# Fritzing sketch EsquemaFritzing (saved by Fritzing 0.9.9b)
breadboards: 2

parts:
  U1 = ESP8266 NodeMCU LoLin module
  DHT1 = DHT11 Humitidy and Temperature Sensor
  J1 = Basic Servo
  V1 = DC Power [voltage=5]

nets:
  N1: U1.D3, J1.pulse
  N2: U1.D4, DHT1.DATA
  3V3: U1.3V3, DHT1.VDD
  GND: U1.GND, DHT1.GND, J1.gnd, V1.V-
  VIN: U1.Vin, J1.vcc, V1.V+

custom parts:
  ESP8266 NodeMCU LoLin module: ESP8266 based NodeMCU
  DHT11 Humitidy and Temperature Sensor: DHT11 Humidity and Temperature Sensor
